# Fritzing sketch board (saved by Fritzing 0.9.2b)
circuit board: 8.46667cm x 5.64444cm
breadboards: 1

parts:
  WeMos_D1_Mini1 = WeMos D1 Mini
  LED1 = LED - 3mm [color="Red (635nm)" package="3 mm [THT]"]
  M1 = BME280
  S3 = Pushbutton [package="[SMD]"]
  R2 = Resistor [tolerance=±5% resistance=1k package=THT]
  LED2 = LED - 3mm [color="Green (560nm)" package="3 mm [THT]"]
  R1 = Resistor [tolerance=±5% resistance=3.3k package=THT]
  R3 = Resistor [tolerance=±5% resistance=1k package=THT]

nets:
  3V3: WeMos_D1_Mini1.3V3, M1.VIN, S3.Pin_1, S3.Pin_2, R2.Pin_1, R1.Pin_1
  N1: WeMos_D1_Mini1.D0, WeMos_D1_Mini1.RST
  N2: WeMos_D1_Mini1.D1, M1.SCL
  N3: WeMos_D1_Mini1.D2, M1.SDA
  N4: WeMos_D1_Mini1.D5, LED2.cathode
  N5: WeMos_D1_Mini1.D6, LED1.cathode
  N6: WeMos_D1_Mini1.D8, S3.Pin_3, S3.Pin_4, R3.Pin_0
  N7: WeMos_D1_Mini1.G, M1.GND, R3.Pin_1
  N8: LED1.anode, R1.Pin_0
  N9: R2.Pin_0, LED2.anode

custom parts:
  WeMos D1 Mini: The D1 mini is a mini wifi board based on ESP-8266EX.
  BME280: Temperature Humidity Barometric presure Sensor
